// Logisim project 16 Bit ALU + Memory Logisim.circ as structural Verilog: 11 circuits, main circuit Half Adder
module Half_Adder (
  input  in_1,
  input  in_2,
  output out_3,
  output out_4
);

  xor XOR (out_3, in_1, in_2);
  and AND (out_4, in_1, in_2);
endmodule

module Full_Adder (
  input  in_1,
  input  in_2,
  input  in_3,
  output out_4,
  output out_5
);

  wire half_adder_1_out_3, half_adder_1_out_4, half_adder_2_out_4;

  Half_Adder half_adder_1 (.in_1(in_1), .in_2(in_2), .out_3(half_adder_1_out_3), .out_4(half_adder_1_out_4));
  Half_Adder half_adder_2 (.in_1(half_adder_1_out_3), .in_2(in_3), .out_3(out_4), .out_4(half_adder_2_out_4));
  or or_1 (out_5, half_adder_1_out_4, half_adder_2_out_4);
endmodule

module _16_Bit_Adder_Subtractor (
  input  [15:0] A,
  input  [15:0] B,
  input  Mode,
  output [15:0] Sum,
  output Carry_Out
);

  wire full_adder_1_out_5, full_adder_2_out_5, full_adder_3_out_5, full_adder_4_out_5, full_adder_5_out_5,
       full_adder_6_out_5, full_adder_7_out_5, full_adder_8_out_5, full_adder_9_out_5, full_adder_10_out_5,
       full_adder_11_out_5, full_adder_12_out_5, full_adder_13_out_5, full_adder_14_out_5,
       full_adder_15_out_5, xor_1_out, xor_2_out, xor_3_out, xor_4_out, xor_5_out, xor_6_out, xor_7_out,
       xor_8_out, xor_9_out, xor_10_out, xor_11_out, xor_12_out, xor_13_out, xor_14_out, xor_15_out,
       xor_16_out;

  xor xor_1 (xor_1_out, B[0], Mode);
  xor xor_2 (xor_2_out, B[1], Mode);
  xor xor_3 (xor_3_out, B[2], Mode);
  xor xor_4 (xor_4_out, B[3], Mode);
  xor xor_5 (xor_5_out, B[4], Mode);
  xor xor_6 (xor_6_out, B[5], Mode);
  xor xor_7 (xor_7_out, B[6], Mode);
  xor xor_8 (xor_8_out, B[7], Mode);
  Full_Adder full_adder_1 (.in_1(Mode), .in_2(A[0]), .in_3(xor_1_out), .out_4(Sum[0]), .out_5(full_adder_1_out_5));
  Full_Adder full_adder_2 (
    .in_1(full_adder_1_out_5), .in_2(A[1]), .in_3(xor_2_out), .out_4(Sum[1]), .out_5(full_adder_2_out_5));
  Full_Adder full_adder_3 (
    .in_1(full_adder_2_out_5), .in_2(A[2]), .in_3(xor_3_out), .out_4(Sum[2]), .out_5(full_adder_3_out_5));
  Full_Adder full_adder_4 (
    .in_1(full_adder_3_out_5), .in_2(A[3]), .in_3(xor_4_out), .out_4(Sum[3]), .out_5(full_adder_4_out_5));
  Full_Adder full_adder_5 (
    .in_1(full_adder_4_out_5), .in_2(A[4]), .in_3(xor_5_out), .out_4(Sum[4]), .out_5(full_adder_5_out_5));
  Full_Adder full_adder_6 (
    .in_1(full_adder_5_out_5), .in_2(A[5]), .in_3(xor_6_out), .out_4(Sum[5]), .out_5(full_adder_6_out_5));
  Full_Adder full_adder_7 (
    .in_1(full_adder_6_out_5), .in_2(A[6]), .in_3(xor_7_out), .out_4(Sum[6]), .out_5(full_adder_7_out_5));
  Full_Adder full_adder_8 (
    .in_1(full_adder_7_out_5), .in_2(A[7]), .in_3(xor_8_out), .out_4(Sum[7]), .out_5(full_adder_8_out_5));
  xor xor_9 (xor_9_out, B[8], Mode);
  xor xor_10 (xor_10_out, B[9], Mode);
  xor xor_11 (xor_11_out, B[10], Mode);
  xor xor_12 (xor_12_out, B[11], Mode);
  xor xor_13 (xor_13_out, B[12], Mode);
  xor xor_14 (xor_14_out, B[13], Mode);
  xor xor_15 (xor_15_out, B[14], Mode);
  xor xor_16 (xor_16_out, B[15], Mode);
  Full_Adder full_adder_9 (
    .in_1(full_adder_8_out_5), .in_2(A[8]), .in_3(xor_9_out), .out_4(Sum[8]), .out_5(full_adder_9_out_5));
  Full_Adder full_adder_10 (
    .in_1(full_adder_9_out_5), .in_2(A[9]), .in_3(xor_10_out), .out_4(Sum[9]), .out_5(full_adder_10_out_5));
  Full_Adder full_adder_11 (
    .in_1(full_adder_10_out_5), .in_2(A[10]), .in_3(xor_11_out), .out_4(Sum[10]), .out_5(full_adder_11_out_5));
  Full_Adder full_adder_12 (
    .in_1(full_adder_11_out_5), .in_2(A[11]), .in_3(xor_12_out), .out_4(Sum[11]), .out_5(full_adder_12_out_5));
  Full_Adder full_adder_13 (
    .in_1(full_adder_12_out_5), .in_2(A[12]), .in_3(xor_13_out), .out_4(Sum[12]), .out_5(full_adder_13_out_5));
  Full_Adder full_adder_14 (
    .in_1(full_adder_13_out_5), .in_2(A[13]), .in_3(xor_14_out), .out_4(Sum[13]), .out_5(full_adder_14_out_5));
  Full_Adder full_adder_15 (
    .in_1(full_adder_14_out_5), .in_2(A[14]), .in_3(xor_15_out), .out_4(Sum[14]), .out_5(full_adder_15_out_5));
  Full_Adder full_adder_16 (
    .in_1(full_adder_15_out_5), .in_2(A[15]), .in_3(xor_16_out), .out_4(Sum[15]), .out_5(Carry_Out));
endmodule

// Gates
module AND__OR__NOT__XOR (
  input  [15:0] A,
  input  [15:0] B,
  output [15:0] AND_Output,
  output [15:0] OR_Output,
  output [15:0] NOT_Output,
  output [15:0] XOR_Output
);

  assign AND_Output = A & B;  // AND_Gate and_1, 16 bits wide
  assign OR_Output = A | B;  // OR_Gate or_1, 16 bits wide
  assign NOT_Output = ~A;  // NOT_Gate not_1, 16 bits wide
  assign XOR_Output = A ^ B;  // XOR_Gate xor_1, 16 bits wide
endmodule

module Shifter (
  input  [15:0] Input,
  input  Select,
  output [15:0] Output
);

  wire and_1_out, and_2_out, and_3_out, and_4_out, and_5_out, and_6_out, and_7_out, and_8_out, and_9_out,
       and_10_out, and_11_out, and_12_out, and_13_out, and_14_out, and_15_out, and_16_out, and_17_out,
       and_18_out, and_19_out, and_20_out, and_21_out, and_22_out, and_23_out, and_24_out, and_25_out,
       and_26_out, and_27_out, and_28_out, and_29_out, and_30_out, and_31_out, and_32_out, not_1_out;

  not not_1 (not_1_out, Select);
  and and_1 (and_1_out, not_1_out, Select);
  or or_1 (Output[0], and_1_out, and_4_out);
  and and_2 (and_2_out, Input[0], Select);
  and and_3 (and_3_out, Input[1], Select);
  and and_4 (and_4_out, not_1_out, Input[1]);
  or or_2 (Output[1], and_2_out, and_5_out);
  and and_5 (and_5_out, not_1_out, Input[2]);
  or or_3 (Output[2], and_3_out, and_7_out);
  and and_6 (and_6_out, Input[2], Select);
  and and_7 (and_7_out, not_1_out, Input[3]);
  and and_8 (and_8_out, Input[3], Select);
  or or_4 (Output[3], and_6_out, and_9_out);
  and and_9 (and_9_out, not_1_out, Input[4]);
  or or_5 (Output[4], and_8_out, and_10_out);
  and and_10 (and_10_out, not_1_out, Input[5]);
  and and_11 (and_11_out, Input[4], Select);
  and and_12 (and_12_out, Input[5], Select);
  or or_6 (Output[5], and_11_out, and_13_out);
  and and_13 (and_13_out, not_1_out, Input[6]);
  and and_14 (and_14_out, Input[6], Select);
  or or_7 (Output[6], and_12_out, and_15_out);
  and and_15 (and_15_out, not_1_out, Input[7]);
  and and_16 (and_16_out, Input[7], Select);
  or or_8 (Output[7], and_14_out, and_18_out);
  and and_17 (and_17_out, Input[8], Select);
  and and_18 (and_18_out, not_1_out, Input[8]);
  or or_9 (Output[8], and_16_out, and_19_out);
  and and_19 (and_19_out, not_1_out, Input[9]);
  and and_20 (and_20_out, Input[9], Select);
  or or_10 (Output[9], and_17_out, and_22_out);
  and and_21 (and_21_out, Input[10], Select);
  and and_22 (and_22_out, not_1_out, Input[10]);
  or or_11 (Output[10], and_20_out, and_23_out);
  and and_23 (and_23_out, not_1_out, Input[11]);
  or or_12 (Output[11], and_21_out, and_25_out);
  and and_24 (and_24_out, Input[11], Select);
  and and_25 (and_25_out, not_1_out, Input[12]);
  and and_26 (and_26_out, Input[12], Select);
  or or_13 (Output[12], and_24_out, and_27_out);
  and and_27 (and_27_out, not_1_out, Input[13]);
  or or_14 (Output[13], and_26_out, and_29_out);
  and and_28 (and_28_out, Input[13], Select);
  and and_29 (and_29_out, not_1_out, Input[14]);
  and and_30 (and_30_out, Input[14], Select);
  or or_15 (Output[14], and_28_out, and_31_out);
  and and_31 (and_31_out, not_1_out, Input[15]);
  or or_16 (Output[15], and_30_out, and_32_out);
  and and_32 (and_32_out, not_1_out, Input[0]);
endmodule

module _16_bit_ALU (
  input  [15:0] A,
  input  Reset,
  input  [15:0] B,
  input  Subtractor,
  input  [1:0] Select_Mode,
  input  [1:0] Select,
  input  Left_Shift,
  output Carry,
  output [15:0] OUTPUT
);

  wire not_1_out;
  wire [15:0] Adder_Sub_sum, and_or_not_xor_1_and_output, and_or_not_xor_1_not_output,
       and_or_not_xor_1_or_output, and_or_not_xor_1_xor_output, bit_extender_1_out, multiplexer_1_out,
       multiplexer_2_out, Shifter_output;

  Shifter Shifter (.Select(Left_Shift), .Output(Shifter_output), .Input(A));
  _16_Bit_Adder_Subtractor Adder_Sub (.A(A), .B(B), .Mode(Subtractor), .Sum(Adder_Sub_sum), .Carry_Out(Carry));
  AND__OR__NOT__XOR and_or_not_xor_1 (
    .A(A), .B(B), .AND_Output(and_or_not_xor_1_and_output), .OR_Output(and_or_not_xor_1_or_output),
    .NOT_Output(and_or_not_xor_1_not_output), .XOR_Output(and_or_not_xor_1_xor_output));
  Multiplexer #(.select(2), .width(16), .enable("false")) multiplexer_1 (
    .in0(and_or_not_xor_1_and_output), .in1(and_or_not_xor_1_or_output), .in2(and_or_not_xor_1_not_output),
    .in3(and_or_not_xor_1_xor_output), .out(multiplexer_1_out), .sel(Select_Mode));
  not not_1 (not_1_out, Reset);
  assign bit_extender_1_out = {{15{not_1_out}}, not_1_out};  // Bit_Extender bit_extender_1
  Multiplexer #(.select(2), .width(16), .enable("false")) multiplexer_2 (
    .in0(Adder_Sub_sum), .in1(multiplexer_1_out), .in2(Shifter_output), .out(multiplexer_2_out), .sel(Select));  // open: in3
  assign OUTPUT = bit_extender_1_out & multiplexer_2_out;  // AND_Gate and_1, 16 bits wide

  // Notes on the sheet:
  //   AND - 00
  //   OR - 01
  //   NOT - 10
  //   XOR - 11
  //   Logical Gates - 01
  //   Adder/Sub - 00
  //   Shifter - 10
endmodule

module Final_16_Bit_ALU (
  input  Reset,
  input  Subtractor,
  input  [15:0] A,
  input  [15:0] B,
  input  [1:0] Gates,
  input  [1:0] Mode,
  input  Left_Shift,
  output Carry,
  output [15:0] OUTPUT
);

  _16_bit_ALU u_16_bit_alu_1 (
    .A(A), .Reset(Reset), .B(B), .Subtractor(Subtractor), .Select_Mode(Gates), .Select(Mode),
    .Left_Shift(Left_Shift), .Carry(Carry), .OUTPUT(OUTPUT));

  // Notes on the sheet:
  //   Gates
  //   00 = AND
  //   01 = OR
  //   10 = NOT
  //   11 = XOR
  //   Add/Sub
  //   0 = Add
  //   1 = Subtract
  //   10 = Shifter
  //   Mode
  //   00 = Adder/Subtractor
  //   01 = Logical Gates
  //   Shift
  //   0 = Right Shift
  //   1 = Left Shift
endmodule

module _16_Bit_Memory (
  input  Clock,
  input  [15:0] Input,
  output [15:0] Output
);

  D_Flip_Flop d_ff_1 (.clk(Clock), .D(Input[0]), .Q(Output[0]));  // open: Qn, preset, en, reset
  D_Flip_Flop d_ff_2 (.clk(Clock), .D(Input[1]), .Q(Output[1]));  // open: Qn, preset, en, reset
  D_Flip_Flop d_ff_3 (.clk(Clock), .D(Input[2]), .Q(Output[2]));  // open: Qn, preset, en, reset
  D_Flip_Flop d_ff_4 (.clk(Clock), .D(Input[3]), .Q(Output[3]));  // open: Qn, preset, en, reset
  D_Flip_Flop d_ff_5 (.clk(Clock), .D(Input[4]), .Q(Output[4]));  // open: Qn, preset, en, reset
  D_Flip_Flop d_ff_6 (.clk(Clock), .D(Input[5]), .Q(Output[5]));  // open: Qn, preset, en, reset
  D_Flip_Flop d_ff_7 (.clk(Clock), .D(Input[6]), .Q(Output[6]));  // open: Qn, preset, en, reset
  D_Flip_Flop d_ff_8 (.clk(Clock), .D(Input[7]), .Q(Output[7]));  // open: Qn, preset, en, reset
  D_Flip_Flop d_ff_9 (.clk(Clock), .D(Input[8]), .Q(Output[8]));  // open: Qn, preset, en, reset
  D_Flip_Flop d_ff_10 (.clk(Clock), .D(Input[9]), .Q(Output[9]));  // open: Qn, preset, en, reset
  D_Flip_Flop d_ff_11 (.clk(Clock), .D(Input[10]), .Q(Output[10]));  // open: Qn, preset, en, reset
  D_Flip_Flop d_ff_12 (.clk(Clock), .D(Input[11]), .Q(Output[11]));  // open: Qn, preset, en, reset
  D_Flip_Flop d_ff_13 (.clk(Clock), .D(Input[12]), .Q(Output[12]));  // open: Qn, preset, en, reset
  D_Flip_Flop d_ff_14 (.clk(Clock), .D(Input[13]), .Q(Output[13]));  // open: Qn, preset, en, reset
  D_Flip_Flop d_ff_15 (.clk(Clock), .D(Input[14]), .Q(Output[14]));  // open: Qn, preset, en, reset
  D_Flip_Flop d_ff_16 (.clk(Clock), .D(Input[15]), .Q(Output[15]));  // open: Qn, preset, en, reset
endmodule

module _32_X_16_Memory (
  input  Clock,
  input  Reset,
  input  [15:0] Input,
  input  [4:0] Address,
  input  [4:0] Location,
  output [15:0] Output
);

  wire not_1_out;
  wire [15:0] bit_extender_1_out, demultiplexer_1_out0, demultiplexer_1_out1, demultiplexer_1_out2,
       demultiplexer_1_out3, demultiplexer_1_out4, demultiplexer_1_out5, demultiplexer_1_out6,
       demultiplexer_1_out7, demultiplexer_1_out8, demultiplexer_1_out9, demultiplexer_1_out10,
       demultiplexer_1_out11, demultiplexer_1_out12, demultiplexer_1_out13, demultiplexer_1_out14,
       demultiplexer_1_out15, demultiplexer_1_out16, demultiplexer_1_out17, demultiplexer_1_out18,
       demultiplexer_1_out19, demultiplexer_1_out20, demultiplexer_1_out21, demultiplexer_1_out22,
       demultiplexer_1_out23, demultiplexer_1_out24, demultiplexer_1_out25, demultiplexer_1_out26,
       demultiplexer_1_out27, demultiplexer_1_out28, demultiplexer_1_out29, demultiplexer_1_out30,
       demultiplexer_1_out31, multiplexer_1_out, n16_bit_memory_1_output, n16_bit_memory_2_output,
       n16_bit_memory_3_output, n16_bit_memory_4_output, n16_bit_memory_5_output, n16_bit_memory_6_output,
       n16_bit_memory_7_output, n16_bit_memory_8_output, n16_bit_memory_9_output, n16_bit_memory_10_output,
       n16_bit_memory_11_output, n16_bit_memory_12_output, n16_bit_memory_13_output,
       n16_bit_memory_14_output, n16_bit_memory_15_output, n16_bit_memory_16_output,
       n16_bit_memory_17_output, n16_bit_memory_18_output, n16_bit_memory_19_output,
       n16_bit_memory_20_output, n16_bit_memory_21_output, n16_bit_memory_22_output,
       n16_bit_memory_23_output, n16_bit_memory_24_output, n16_bit_memory_25_output,
       n16_bit_memory_26_output, n16_bit_memory_27_output, n16_bit_memory_28_output,
       n16_bit_memory_29_output, n16_bit_memory_30_output, n16_bit_memory_31_output, n16_bit_memory_32_output;

  Demultiplexer #(.select(5), .width(16)) demultiplexer_1 (
    .out0(demultiplexer_1_out0), .out1(demultiplexer_1_out1), .out2(demultiplexer_1_out2),
    .out3(demultiplexer_1_out3), .out4(demultiplexer_1_out4), .out5(demultiplexer_1_out5),
    .out6(demultiplexer_1_out6), .out7(demultiplexer_1_out7), .out8(demultiplexer_1_out8),
    .out9(demultiplexer_1_out9), .out10(demultiplexer_1_out10), .out11(demultiplexer_1_out11),
    .out12(demultiplexer_1_out12), .out13(demultiplexer_1_out13), .out14(demultiplexer_1_out14),
    .out15(demultiplexer_1_out15), .out16(demultiplexer_1_out16), .out17(demultiplexer_1_out17),
    .out18(demultiplexer_1_out18), .out19(demultiplexer_1_out19), .out20(demultiplexer_1_out20),
    .out21(demultiplexer_1_out21), .out22(demultiplexer_1_out22), .out23(demultiplexer_1_out23),
    .out24(demultiplexer_1_out24), .out25(demultiplexer_1_out25), .out26(demultiplexer_1_out26),
    .out27(demultiplexer_1_out27), .out28(demultiplexer_1_out28), .out29(demultiplexer_1_out29),
    .out30(demultiplexer_1_out30), .out31(demultiplexer_1_out31), .in(Input), .sel(Address));  // open: en
  _16_Bit_Memory u_16_bit_memory_1 (.Clock(Clock), .Input(demultiplexer_1_out0), .Output(n16_bit_memory_1_output));
  _16_Bit_Memory u_16_bit_memory_2 (.Clock(Clock), .Input(demultiplexer_1_out1), .Output(n16_bit_memory_2_output));
  _16_Bit_Memory u_16_bit_memory_3 (.Clock(Clock), .Input(demultiplexer_1_out2), .Output(n16_bit_memory_3_output));
  _16_Bit_Memory u_16_bit_memory_4 (.Clock(Clock), .Input(demultiplexer_1_out3), .Output(n16_bit_memory_4_output));
  _16_Bit_Memory u_16_bit_memory_5 (.Clock(Clock), .Input(demultiplexer_1_out4), .Output(n16_bit_memory_5_output));
  _16_Bit_Memory u_16_bit_memory_6 (.Clock(Clock), .Input(demultiplexer_1_out5), .Output(n16_bit_memory_6_output));
  _16_Bit_Memory u_16_bit_memory_7 (.Clock(Clock), .Input(demultiplexer_1_out6), .Output(n16_bit_memory_7_output));
  _16_Bit_Memory u_16_bit_memory_8 (.Clock(Clock), .Input(demultiplexer_1_out7), .Output(n16_bit_memory_8_output));
  _16_Bit_Memory u_16_bit_memory_9 (.Clock(Clock), .Input(demultiplexer_1_out8), .Output(n16_bit_memory_9_output));
  _16_Bit_Memory u_16_bit_memory_10 (.Clock(Clock), .Input(demultiplexer_1_out9), .Output(n16_bit_memory_10_output));
  _16_Bit_Memory u_16_bit_memory_11 (.Clock(Clock), .Input(demultiplexer_1_out10), .Output(n16_bit_memory_11_output));
  _16_Bit_Memory u_16_bit_memory_12 (.Clock(Clock), .Input(demultiplexer_1_out11), .Output(n16_bit_memory_12_output));
  _16_Bit_Memory u_16_bit_memory_13 (.Clock(Clock), .Input(demultiplexer_1_out12), .Output(n16_bit_memory_13_output));
  _16_Bit_Memory u_16_bit_memory_14 (.Clock(Clock), .Input(demultiplexer_1_out13), .Output(n16_bit_memory_14_output));
  _16_Bit_Memory u_16_bit_memory_15 (.Clock(Clock), .Input(demultiplexer_1_out14), .Output(n16_bit_memory_15_output));
  _16_Bit_Memory u_16_bit_memory_16 (.Clock(Clock), .Input(demultiplexer_1_out15), .Output(n16_bit_memory_16_output));
  _16_Bit_Memory u_16_bit_memory_17 (.Clock(Clock), .Input(demultiplexer_1_out16), .Output(n16_bit_memory_17_output));
  _16_Bit_Memory u_16_bit_memory_18 (.Clock(Clock), .Input(demultiplexer_1_out17), .Output(n16_bit_memory_18_output));
  _16_Bit_Memory u_16_bit_memory_19 (.Clock(Clock), .Input(demultiplexer_1_out18), .Output(n16_bit_memory_19_output));
  _16_Bit_Memory u_16_bit_memory_20 (.Clock(Clock), .Input(demultiplexer_1_out19), .Output(n16_bit_memory_20_output));
  _16_Bit_Memory u_16_bit_memory_21 (.Clock(Clock), .Input(demultiplexer_1_out20), .Output(n16_bit_memory_21_output));
  _16_Bit_Memory u_16_bit_memory_22 (.Clock(Clock), .Input(demultiplexer_1_out21), .Output(n16_bit_memory_22_output));
  _16_Bit_Memory u_16_bit_memory_23 (.Clock(Clock), .Input(demultiplexer_1_out22), .Output(n16_bit_memory_23_output));
  _16_Bit_Memory u_16_bit_memory_24 (.Clock(Clock), .Input(demultiplexer_1_out23), .Output(n16_bit_memory_24_output));
  _16_Bit_Memory u_16_bit_memory_25 (.Clock(Clock), .Input(demultiplexer_1_out24), .Output(n16_bit_memory_25_output));
  _16_Bit_Memory u_16_bit_memory_26 (.Clock(Clock), .Input(demultiplexer_1_out25), .Output(n16_bit_memory_26_output));
  _16_Bit_Memory u_16_bit_memory_27 (.Clock(Clock), .Input(demultiplexer_1_out26), .Output(n16_bit_memory_27_output));
  _16_Bit_Memory u_16_bit_memory_28 (.Clock(Clock), .Input(demultiplexer_1_out27), .Output(n16_bit_memory_28_output));
  _16_Bit_Memory u_16_bit_memory_29 (.Clock(Clock), .Input(demultiplexer_1_out28), .Output(n16_bit_memory_29_output));
  _16_Bit_Memory u_16_bit_memory_30 (.Clock(Clock), .Input(demultiplexer_1_out29), .Output(n16_bit_memory_30_output));
  _16_Bit_Memory u_16_bit_memory_31 (.Clock(Clock), .Input(demultiplexer_1_out30), .Output(n16_bit_memory_31_output));
  _16_Bit_Memory u_16_bit_memory_32 (.Clock(Clock), .Input(demultiplexer_1_out31), .Output(n16_bit_memory_32_output));
  Multiplexer #(.select(5), .width(16)) multiplexer_1 (
    .in0(n16_bit_memory_1_output), .in1(n16_bit_memory_2_output), .in2(n16_bit_memory_3_output),
    .in3(n16_bit_memory_4_output), .in4(n16_bit_memory_5_output), .in5(n16_bit_memory_6_output),
    .in6(n16_bit_memory_7_output), .in7(n16_bit_memory_8_output), .in8(n16_bit_memory_9_output),
    .in9(n16_bit_memory_10_output), .in10(n16_bit_memory_11_output), .in11(n16_bit_memory_12_output),
    .in12(n16_bit_memory_13_output), .in13(n16_bit_memory_14_output), .in14(n16_bit_memory_15_output),
    .in15(n16_bit_memory_16_output), .in16(n16_bit_memory_17_output), .in17(n16_bit_memory_18_output),
    .in18(n16_bit_memory_19_output), .in19(n16_bit_memory_20_output), .in20(n16_bit_memory_21_output),
    .in21(n16_bit_memory_22_output), .in22(n16_bit_memory_23_output), .in23(n16_bit_memory_24_output),
    .in24(n16_bit_memory_25_output), .in25(n16_bit_memory_26_output), .in26(n16_bit_memory_27_output),
    .in27(n16_bit_memory_28_output), .in28(n16_bit_memory_29_output), .in29(n16_bit_memory_30_output),
    .in30(n16_bit_memory_31_output), .in31(n16_bit_memory_32_output), .out(multiplexer_1_out), .sel(Location));  // open: en
  not not_1 (not_1_out, Reset);
  assign bit_extender_1_out = {{15{not_1_out}}, not_1_out};  // Bit_Extender bit_extender_1
  assign Output = bit_extender_1_out & multiplexer_1_out;  // AND_Gate and_1, 16 bits wide
endmodule

module ALU___Memory (
  input  Reset,
  input  Clock,
  input  [3:0] Read_Register_1,
  input  Subtractor,
  input  [3:0] Read_Register_2,
  input  [3:0] Write_Register,
  input  [15:0] Write_Data,
  input  Reg_write,
  input  Clock_2,
  input  [1:0] Gates,
  input  Left_Shift,
  input  [1:0] Mode,
  input  mux2,
  input  mux1,
  output Carry,
  output [15:0] Read_data_1,
  output [15:0] Read_data_2,
  output [15:0] Output
);

  wire [4:0] bit_extender_2_out;
  wire [15:0] bit_extender_1_out, final_16_bit_alu_1_output, multiplexer_1_out, n32_x_16_memory_1_output;

  assign bit_extender_1_out = {{12{1'b0}}, Write_Register};  // Bit_Extender bit_extender_1
  _16_Bit_Register u_16_bit_register_1 (
    .Write_Register(Write_Register), .Read_Register_1(Read_Register_1), .Read_Register_2(Read_Register_2),
    .Write_Data(Write_Data), .Clock(Clock_2), .Reg_Write(Reg_write), .Read_data_1(Read_data_1),
    .Read_data_2(Read_data_2));
  Multiplexer #(.width(16), .enable("false")) multiplexer_1 (
    .in0(Read_data_2), .in1(bit_extender_1_out), .out(multiplexer_1_out), .sel(mux1));
  Final_16_Bit_ALU final_16_bit_alu_1 (
    .Reset(Reset), .A(Read_data_1), .B(multiplexer_1_out), .Gates(Gates), .Mode(Mode),
    .Subtractor(Subtractor), .Left_Shift(Left_Shift), .Carry(Carry), .OUTPUT(final_16_bit_alu_1_output));
  Bit_Extender #(.in_width(16), .out_width(5)) bit_extender_2 (
    .in(final_16_bit_alu_1_output), .out(bit_extender_2_out));
  _32_X_16_Memory u_32_x_16_memory_1 (
    .Clock(Clock), .Reset(Reset), .Input(multiplexer_1_out), .Address(bit_extender_2_out),
    .Output(n32_x_16_memory_1_output), .Location(bit_extender_2_out));
  Multiplexer #(.width(16), .enable("false")) multiplexer_2 (
    .in0(n32_x_16_memory_1_output), .in1(final_16_bit_alu_1_output), .out(Output), .sel(mux2));

  // Notes on the sheet:
  //   Gates
  //   00 = AND
  //   01 = OR
  //   10 = NOT
  //   11 = XOR
  //   Add/Sub
  //   0 = Add
  //   1 = Subtract
  //   Mode
  //   00 = Adder/Subtractor
  //   01 = Logical Gates
  //   10 = Shifter
  //   Shift
  //   0 = Right Shift
  //   1 = Left Shift
endmodule

module _16_Bit_Register (
  input  [3:0] Write_Register,
  input  [3:0] Read_Register_1,
  input  [3:0] Read_Register_2,
  input  [15:0] Write_Data,
  input  Clock,
  input  Reg_Write,
  output [15:0] Read_data_1,
  output [15:0] Read_data_2
);

  wire and_1_out, and_2_out, and_3_out, and_4_out, and_5_out, and_6_out, and_7_out, and_8_out, and_9_out,
       and_10_out, and_11_out, and_12_out, and_13_out, and_14_out, and_15_out, and_16_out, decoder_1_out0,
       decoder_1_out1, decoder_1_out2, decoder_1_out3, decoder_1_out4, decoder_1_out5, decoder_1_out6,
       decoder_1_out7, decoder_1_out8, decoder_1_out9, decoder_1_out10, decoder_1_out11, decoder_1_out12,
       decoder_1_out13, decoder_1_out14, decoder_1_out15;
  wire [15:0] register_1_q, register_2_q, register_3_q, register_4_q, register_5_q, register_6_q,
       register_7_q, register_8_q, register_9_q, register_10_q, register_11_q, register_12_q, register_13_q,
       register_14_q, register_15_q, register_16_q;

  Decoder #(.select(4)) decoder_1 (
    .out0(decoder_1_out0), .out1(decoder_1_out1), .out2(decoder_1_out2), .out3(decoder_1_out3),
    .out4(decoder_1_out4), .out5(decoder_1_out5), .out6(decoder_1_out6), .out7(decoder_1_out7),
    .out8(decoder_1_out8), .out9(decoder_1_out9), .out10(decoder_1_out10), .out11(decoder_1_out11),
    .out12(decoder_1_out12), .out13(decoder_1_out13), .out14(decoder_1_out14), .out15(decoder_1_out15),
    .sel(Write_Register));  // open: en
  and and_1 (and_1_out, decoder_1_out0, Reg_Write);
  and and_2 (and_2_out, decoder_1_out1, Reg_Write);
  and and_3 (and_3_out, decoder_1_out2, Reg_Write);
  and and_4 (and_4_out, decoder_1_out3, Reg_Write);
  and and_5 (and_5_out, decoder_1_out4, Reg_Write);
  and and_6 (and_6_out, decoder_1_out5, Reg_Write);
  and and_7 (and_7_out, decoder_1_out6, Reg_Write);
  and and_8 (and_8_out, decoder_1_out7, Reg_Write);
  Register #(.width(16)) register_1 (.D(Write_Data), .Q(register_1_q), .clk(Clock), .clr(and_1_out));  // open: en
  Register #(.width(16)) register_2 (.D(Write_Data), .Q(register_2_q), .clk(Clock), .clr(and_2_out));  // open: en
  Register #(.width(16)) register_3 (.D(Write_Data), .Q(register_3_q), .clk(Clock), .clr(and_3_out));  // open: en
  Register #(.width(16)) register_4 (.D(Write_Data), .Q(register_4_q), .clk(Clock), .clr(and_4_out));  // open: en
  Register #(.width(16)) register_5 (.D(Write_Data), .Q(register_5_q), .clk(Clock), .clr(and_5_out));  // open: en
  Register #(.width(16)) register_6 (.D(Write_Data), .Q(register_6_q), .clk(Clock), .clr(and_6_out));  // open: en
  Register #(.width(16)) register_7 (.D(Write_Data), .Q(register_7_q), .clk(Clock), .clr(and_7_out));  // open: en
  Register #(.width(16)) register_8 (.D(Write_Data), .Q(register_8_q), .clk(Clock), .clr(and_8_out));  // open: en
  and and_9 (and_9_out, decoder_1_out8, Reg_Write);
  and and_10 (and_10_out, decoder_1_out9, Reg_Write);
  and and_11 (and_11_out, decoder_1_out10, Reg_Write);
  and and_12 (and_12_out, decoder_1_out11, Reg_Write);
  and and_13 (and_13_out, decoder_1_out12, Reg_Write);
  and and_14 (and_14_out, decoder_1_out13, Reg_Write);
  and and_15 (and_15_out, decoder_1_out14, Reg_Write);
  and and_16 (and_16_out, decoder_1_out15, Reg_Write);
  Register #(.width(16)) register_9 (.D(Write_Data), .Q(register_9_q), .clk(Clock), .clr(and_9_out));  // open: en
  Register #(.width(16)) register_10 (.D(Write_Data), .Q(register_10_q), .clk(Clock), .clr(and_10_out));  // open: en
  Register #(.width(16)) register_11 (.D(Write_Data), .Q(register_11_q), .clk(Clock), .clr(and_11_out));  // open: en
  Register #(.width(16)) register_12 (.D(Write_Data), .Q(register_12_q), .clk(Clock), .clr(and_12_out));  // open: en
  Register #(.width(16)) register_13 (.D(Write_Data), .Q(register_13_q), .clk(Clock), .clr(and_13_out));  // open: en
  Register #(.width(16)) register_14 (.D(Write_Data), .Q(register_14_q), .clk(Clock), .clr(and_14_out));  // open: en
  Register #(.width(16)) register_15 (.D(Write_Data), .Q(register_15_q), .clk(Clock), .clr(and_15_out));  // open: en
  Register #(.width(16)) register_16 (.D(Write_Data), .Q(register_16_q), .clk(Clock), .clr(and_16_out));  // open: en
  Multiplexer #(.select(4), .width(16)) multiplexer_1 (
    .in0(register_1_q), .in1(register_2_q), .in2(register_3_q), .in3(register_4_q), .in4(register_5_q),
    .in5(register_6_q), .in6(register_7_q), .in7(register_8_q), .in8(register_9_q), .in9(register_10_q),
    .in10(register_11_q), .in11(register_12_q), .in12(register_13_q), .in13(register_14_q),
    .in14(register_15_q), .in15(register_16_q), .out(Read_data_1), .sel(Read_Register_1));  // open: en
  Multiplexer #(.select(4), .width(16)) multiplexer_2 (
    .in0(register_1_q), .in1(register_2_q), .in2(register_3_q), .in3(register_4_q), .in4(register_5_q),
    .in5(register_6_q), .in6(register_7_q), .in7(register_8_q), .in8(register_9_q), .in9(register_10_q),
    .in10(register_11_q), .in11(register_12_q), .in12(register_13_q), .in13(register_14_q),
    .in14(register_15_q), .in15(register_16_q), .out(Read_data_2), .sel(Read_Register_2));  // open: en
endmodule
